# Fritzing sketch Ardunio drums  (saved by Fritzing 1.0.6)
breadboards: 2

parts:
  Part1 = Arduino Mega 2560 (Rev3)
  R1 = Resistor [tolerance=±5% resistance=220 package="2512 [SMD]"]
  LED2 = LED - 3mm [color="Blue (525nm)" current=0.030A package="3 mm [THT]"]
  LED3 = LED - 3mm [color="Red (633nm)" current=0.030A package="3 mm [THT]"]
  LED4 = LED - 3mm [color="Blue (525nm)" current=0.030A package="3 mm [THT]"]
  LED5 = LED - 3mm [color="Red (633nm)" current=0.030A package="3 mm [THT]"]
  LED6 = LED - 3mm [color="Red (633nm)" current=0.030A package="3 mm [THT]"]
  R2 = Resistor [tolerance=±5% resistance=1M package="2512 [SMD]"]
  R3 = Resistor [tolerance=±5% resistance=1M package="2512 [SMD]"]
  R4 = Resistor [tolerance=±5% resistance=1M package="2512 [SMD]"]
  R5 = Resistor [tolerance=±5% resistance=1M package="2512 [SMD]"]
  R6 = Resistor [tolerance=±5% resistance=1M package="2512 [SMD]"]
  Piezoelectric_Sensor1 = Piezoelectric Sensor
  Piezoelectric_Sensor2 = Piezoelectric Sensor
  Piezoelectric_Sensor3 = Piezoelectric Sensor
  Piezoelectric_Sensor4 = Piezoelectric Sensor
  Piezoelectric_Sensor5 = Piezoelectric Sensor

nets:
  N1: Part1.A0, R6.Pin_0, Piezoelectric_Sensor5.VCC
  N2: Part1.A1, R5.Pin_0, Piezoelectric_Sensor4.VCC
  N3: Part1.A2, R4.Pin_0, Piezoelectric_Sensor3.VCC
  N4: Part1.A3, R3.Pin_0, Piezoelectric_Sensor2.VCC
  N5: Part1.A4, R2.Pin_0, Piezoelectric_Sensor1.VCC
  N6: Part1.D13_PWM, LED4.anode
  N7: Part1.D12_PWM, LED2.anode
  GND: Part1.GND, R1.Pin_0, R2.Pin_1, R3.Pin_1, R4.Pin_1, R5.Pin_1, R6.Pin_1, Piezoelectric_Sensor1.GND, Piezoelectric_Sensor2.GND, Piezoelectric_Sensor3.GND, Piezoelectric_Sensor4.GND, Piezoelectric_Sensor5.GND
  N8: Part1.D2_PWM, LED6.anode
  N9: Part1.D3_PWM, LED5.anode
  N10: Part1.D4_PWM, LED3.anode
  N11: R1.Pin_1, LED2.cathode, LED3.cathode, LED4.cathode, LED5.cathode, LED6.cathode

custom parts:
  Piezoelectric Sensor: Piezoelectric sensor.
